# Fritzing sketch PI3_RF01D (saved by Fritzing 0.9.3b)
circuit board: 8.47cm x 5.64444cm
breadboards: 2

parts:
  R3 = Resistor [tolerance=±5% resistance=470 package=THT]
  C1 = Ceramic Capacitor [capacitance=100nF package="100 mil [THT, multilayer]"]
  LED1 = LED - 5mm [color="Red (633nm)" package="5 mm [THT]"]
  R4 = Resistor [tolerance=±5% resistance=470 package=THT]
  Raspberry_Pi2 = Raspberry Pi 2
  R2 = Resistor [tolerance=±5% resistance=1k package=THT]
  R1 = Resistor [tolerance=±5% resistance=1k package=THT]
  LED2 = LED - 5mm [color="Green (570nm)" package="5 mm [THT]"]
  RFID1 = RF01D

nets:
  N1: R3.Pin_0, LED1.anode
  N2: R3.Pin_1, Raspberry_Pi2.GPIO27
  5V: C1.0, Raspberry_Pi2.5V, RFID1.Vcc
  GND: C1.1, LED1.cathode, Raspberry_Pi2.GND, R1.Pin_0, LED2.cathode, RFID1.D_S1, RFID1.D_S2, RFID1.GND
  N3: R4.Pin_0, LED2.anode
  N4: R4.Pin_1, Raspberry_Pi2.GPIO22
  N5: Raspberry_Pi2.GPIO17, R2.Pin_0, R1.Pin_1
  N6: Raspberry_Pi2.GPIO15, RFID1.TXD
  N7: R2.Pin_1, RFID1.Relay
